# Fritzing sketch wiring_diagram (saved by Fritzing 0.9.3b)

parts:
  Mod1 = Raspberry Pi 4B
  J1 = Basic Servo
  PWM1 = PCA9685 16x12-bit PWM Breakout
  JACK1 = 2.1mm Barrel Jack with Terminal Block
  J2 = Basic Servo
  J3 = Basic Servo
  J4 = Basic Servo
  S3 = Round Pushbutton
  S2 = Round Pushbutton

nets:
  N1: Mod1.3V3, PWM1.no_name_yet#505
  N2: Mod1.GPIO2, PWM1.no_name_yet#504
  N3: Mod1.GPIO3, PWM1.no_name_yet#503
  GND: Mod1.GND, J1.gnd, PWM1.no_name_yet#501, PWM1.no_name_yet#701, PWM1.no_name_yet#1000, PWM1.no_name_yet#1001, PWM1.no_name_yet#1002, PWM1.no_name_yet#1003, JACK1.NEG, J2.gnd, J3.gnd, J4.gnd, S3.leg1, S2.leg1
  N4: Mod1.GPIO5, S3.leg0
  N5: Mod1.GPIO13, S2.leg0
  VCC: J1.vcc, PWM1.no_name_yet#100, PWM1.no_name_yet#101, PWM1.no_name_yet#102, PWM1.no_name_yet#103, PWM1.no_name_yet#706, JACK1.POS, J2.vcc, J3.vcc, J4.vcc
  N6: J1.pulse, PWM1.no_name_yet#1
  N7: PWM1.no_name_yet#0, J4.pulse
  N8: PWM1.no_name_yet#2, J2.pulse
  N9: PWM1.no_name_yet#3, J3.pulse

notes:
  Motor Power Supply
  5V - 2A
  Left arm motor
  HDMI to LCD screen
  RPi Power Supply
  5V - 3A
  USB to LCD screen Power
  Audio Jack to Speaker
  USB to Speaker charge
  Left antenna motor
  Right arm motor
  Right antenna motor
  Right button
  Left button
